# Fritzing sketch esp32_OLED_poti (saved by Fritzing 1.0.3b)

parts:
  U1 = ESP32-WROOM-32D-NodeMCU
  OLED1 = SSD1306 0.96in 128x64 I2C Monochrome OLED Display
  R1 = Rotary Potentiometer (Small) [maximum_resistance=100kΩ knob_status=50% power=0.5W package=THT]
  R2 = Rotary Potentiometer (Small) [maximum_resistance=100kΩ knob_status=50% power=0.5W package=THT]
  C1 = Capacitor Polarized [package=cpol-radial-100uf-25v]
  C2 = Capacitor Polarized [package=cpol-radial-100uf-25v]  # not connected
  C3 = Capacitor Polarized [package=cpol-radial-100uf-25v]  # not connected

nets:
  3.3V: U1.3.3V, OLED1.VCC
  N1: U1.EN, C1.-
  N2: U1.SN, R1.wiper
  N3: U1.G34, R2.wiper
  N4: U1.GND#44, R1.leg2, R2.leg2
  N5: U1.G21, OLED1.SDA
  N6: U1.G22, OLED1.SCL
  N7: U1.GND#50, OLED1.GND

notes:
  10 uF
  5K
  Availability: Breadboard Only
  Date / State: 15.08.24 Devel Team: Yannick Koß / C. Koß
  Description: ESP32 --> 2xPoti --> OLED --> BTserial --> PC(COM) interface
  Compatibility:
  serialBT-Datatransfer to AI-Anomaly-Detection-Module
  10 uF for the Programming ISSUE - we do not need to press the "boot" button!
  1 uF to flatten the ADC values of the poti mesurements!
  Code:
  python: D:/ALL_PROJECT/a_Factory/_AnomalyTF/py39tfe/ad_BT_serial_dataTransfer
  ESP32: D:\ALL_PROJECT\VS_vMicro_ESP\ES32_2024\simpleWifiScan\btSerial_Python
  OLED SSD1306
  we use ESP32 WROOM
  Control-Module (Density / Reconstruction Acurancy) for the AI ​​Anomaly Detection Project
  1 uF
  GND
